# Fritzing sketch Air_quality (saved by Fritzing 0.9.3b)
breadboards: 1

parts:
  Part2 = Arduino Pro Mini v13
  Part3 = Bluetooth HM-10 Module
  TD-er1 = MH-Z19 CO2 sensor [part_number=MH-Z19]
  RHT1 = Humidity and Temperature Sensor SH-20
  Part4 = Adafruit BMP180

nets:
  N1: Part2.A4, Part4.SCL
  N2: Part2.A5, Part4.SDA
  GND: Part2.GND, Part3.GND, TD-er1.GND, RHT1.GND_1, Part4.GND
  VCC: Part2.VCC, Part3.VCC, TD-er1.Vin, RHT1.Vcc, Part4.+3V3
  N3: Part2.D11_PWM/MOSI, TD-er1.RX
  N4: Part2.D10_PWM/SS, TD-er1.TX
  N5: Part2.D3_PWM, Part3.RXD
  N6: Part2.D2, Part3.TXD

custom parts:
  Humidity and Temperature Sensor SH-20: Digital relative humidity & temperature sensor SH-20
  Adafruit BMP180: This precision sensor from Bosch is the best low-cost sensing solution for measuring barometric pressure and temperature. Because pressure changes with altitude you can also use it as an altimeter! The sensor is soldered onto a PCB with a 3.3V regulator, I2C level shifter and pull-up resistors on the I2C pins. The BMP180 is the next-generation of sensors from Bosch, and replaces the BMP085.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
